// Digital circuit DraftDesignV2.dig as structural Verilog
module DraftDesignV2 (
  input  clk,
  input  reset,
  input  [1:0] C
);

  wire a0, and_2_out, and_3_out, and_4_out, and_5_out, and_6_out, green, invert, not_2_out, not_3_out,
       or_2_out, or_3_out, or_4_out, or_5_out, Q0_t, Q1, Q1_t, Q2, Q2_t, red, xor_1_out;
  wire [3:0] alu_1_y, four_bit_reg_1_q;

  or or_1 (a0, Q1, Q2);
  and and_1 (green, Q2_t, Q1_t);
  not not_1 (red, green);
  or or_2 (or_2_out, C[1], not_2_out);
  not not_2 (not_2_out, C[0]);
  or or_3 (or_3_out, Q1, Q2);
  alu alu_1 (
    .a({3'b000, a0}), .b(four_bit_reg_1_q), .invert(invert), .arith(1'b1), .pass(1'b0), .cin(1'b0),
    .y(alu_1_y));  // open: cout, overfl
  xor xor_1 (xor_1_out, C[0], C[1]);
  not not_3 (not_3_out, C[0]);
  or or_4 (or_4_out, xor_1_out, Q2);
  and and_2 (and_2_out, or_3_out, invert);
  and and_3 (and_3_out, Q2_t, Q1_t, invert, or_2_out);
  and and_4 (and_4_out, Q2_t, Q1_t, Q0_t, C[1], not_3_out);
  four_bit_reg four_bit_reg_1 (.d(alu_1_y), .enable(1'b1), .reset(reset), .clk(clk), .q(four_bit_reg_1_q));
  and and_5 (and_5_out, C[0], C[1], Q2_t, Q1_t);
  and and_6 (and_6_out, or_4_out, Q1_t);
  or or_5 (or_5_out, and_2_out, and_3_out, and_4_out);
  LED led_1 (.in(red));
  LED led_2 (.in(green));
  D_FF_AS D2 (.Set(1'b0), .D(and_5_out), .C(clk), .Clr(reset), .Q(Q2), .nQ(Q2_t));
  D_FF_AS D1 (.Set(1'b0), .D(and_6_out), .C(clk), .Clr(reset), .Q(Q1), .nQ(Q1_t));
  D_FF_AS D0 (.Set(1'b0), .D(or_5_out), .C(clk), .Clr(reset), .Q(invert), .nQ(Q0_t));
  Seven_Seg_Hex seven_seg_hex_1 (.d(four_bit_reg_1_q), .dp(1'b0));

  // Other names for the same wires on the sheet: Q0 = invert
endmodule
