// Digital circuit full_adder.dig as structural Verilog
module full_adder (
  input  a,
  input  b,
  input  cin,
  output sum,
  output cout
);

  wire and_1_out, and_2_out, and_3_out;

  xor xor_1 (sum, a, b, cin);
  and and_1 (and_1_out, cin, a);
  and and_2 (and_2_out, cin, b);
  and and_3 (and_3_out, b, a);
  or or_1 (cout, and_1_out, and_2_out, and_3_out);
endmodule
